# Fritzing sketch CAD_drawing (saved by Fritzing 0.9.5d)
breadboards: 1

parts:
  5mm赤外線LED = LTE-302 [part_number=OSI5FU5111C-40 package=lte-302]
  U1 = SWITCH_SPDT [package=kps-1290]
  Mod1 = Raspberry Pi 4B
  IC1 = Rasberry Pi NIOR Camera [chip_label=IC package="DIP (Dual Inline) [THT]"]  # not connected
  3mm黄緑色LED = smd LED [color="Green (570nm)" part_number=OSG8HA3Z74A package="0805 [SMD]"]
  R1 = Resistor [tolerance=±5% resistance=100 package="0805 [SMD]"]
  R2 = Resistor [tolerance=±5% resistance=100 package="0805 [SMD]"]
  NchパワーMOSFET = MOSFET-NCHANNEL [part_number="60V25A 2SK2232\n" package=to220v]
  5mm赤外線LED_2 = LTE-302 [part_number=OSI5FU5111C-40 package=lte-302]
  5mm赤外線LED1 = LTE-302 [part_number=OSI5FU5111C-40 package=lte-302]
  R4 = Resistor [tolerance=±5% resistance=100 package="0603 [SMD]"]
  R3 = Resistor [tolerance=±5% resistance=100 package="0805 [SMD]"]
  赤外線リモコン受信モジュール = TSOP312.., 314.. [part_number="OSRB38C9AA\n" package=THT]
  R5 = Resistor [tolerance=±5% resistance=10k package="0805 [SMD]"]
  S1 = Momentary Switch [package=ksa_sealed_tac_switch]

nets (from the schematic view):
  N1: 5mm赤外線LED.A, R2.Pin_1
  N2: 5mm赤外線LED.C, 3mm黄緑色LED.cathode, NchパワーMOSFET.D, 5mm赤外線LED_2.C, 5mm赤外線LED1.C
  N3: U1.O, R1.Pin_0, R2.Pin_0, R4.Pin_0, R3.Pin_0
  N4: U1.P, Mod1.5V
  N5: U1.S, 赤外線リモコン受信モジュール.Vs
  N6: Mod1.GPIO23, 赤外線リモコン受信モジュール.Data
  GND: Mod1.GND, NchパワーMOSFET.S, 赤外線リモコン受信モジュール.GND, R5.Pin_0
  N7: Mod1.GPIO25, NchパワーMOSFET.G, R5.Pin_1
  N8: 3mm黄緑色LED.anode, S1.3, S1.4
  N9: R1.Pin_1, S1.1, S1.2
  N10: 5mm赤外線LED_2.A, R4.Pin_1
  N11: 5mm赤外線LED1.A, R3.Pin_1

custom parts:
  Rasberry Pi NIOR Camera: Camera
